# Fritzing sketch power_supply (saved by Fritzing 1.0.2b)
# 18650 Li-ion Battery: CC-BY Dr Kristofer Chan, King's College London/Remote-research.org
breadboards: 1

parts:
  Mod1 = 2S-BMS
  BAT1 = 18650 Li-ion Battery [package=battery-18650]
  BAT2 = 18650 Li-ion Battery [package=battery-18650]
  D1 = Rectifier Diode [part_number=1N4001 package="300 mil [THT]"]
  LED1 = LED - 5mm [color="Red (633nm)" current=0.030A package="5 mm [THT]"]
  R1 = Resistor [tolerance=±5% power=0.25W resistance=470 package=THT]
  R2 = Resistor [tolerance=±5% power=0.25W resistance=33 package=THT]
  J1 = Power Jack [package=power_jack_pth]
  S1 = Toggle Switch [package=THT]
  D2 = Rectifier Diode [part_number=1N4001 package="300 mil [THT]"]
  Componente1 = Arduino Nano (Rev3.0)
  D3 = Rectifier Diode [part_number=1N4001 package="300 mil [THT]"]

nets:
  N1: Mod1.pin1, BAT1.+
  N2: Mod1.pin2, BAT2.-
  N3: Mod1.pin3#2, LED1.cathode, J1.GND
  N4: Mod1.pin3#3, R2.Pin_1, S1.L2
  N5: Mod1.pin3#4, BAT1.-, BAT2.+
  N6: D1.cathode, R2.Pin_0
  N7: D1.anode, R1.Pin_1, J1.PWR
  N8: LED1.anode, R1.Pin_0
  N9: J1.GNDBREAK, Componente1.GND
  N10: S1.COM, D2.anode
  N11: D2.cathode, D3.anode
  N12: Componente1.VIN, D3.cathode

notes:
  ON
  OFF
  R1
  R2
  D1
  D2
  R1 33R x 5W fio
  D1, D2 e D3 1N4007
  R2 470R ou 390R x 1/8 W
  OUTPUT 7,4 V / 8,4 V
  Entrada no J1
  12V x 1A
  J1
  BMS 2S
  2 x (3,7 V x 2200mA)
  D3

custom parts:
  2S-BMS: 2S-BMS LIPO battery charger / protection unit. Note pcb does not match the board as it will likely connect with wires, so pcb is 5 pads suitable for .1in header pins.
  18650 Li-ion Battery: 18650 li-ion Battery Standard 18650 battery with interactive connectors Creative Common Attribution 4.0 International (CC-BY 4.0) license. Any use of this part requires attribution of Dr Kristofer Chan, Department of Geography, King's College London. Contact kristofer.chan [at] kcl.ac.uk OR kris [at] remote-research.org for further information.
