# Fritzing sketch receptor_lora_blocos (saved by Fritzing 1.0.2b)
breadboards: 1

parts:
  Componente1 = Arduino Nano (Rev3.0)
  A1 = NEO-6M GPS Module [part_number=GY-GPS6MV2]
  LED1 = smd LED [color="Red (633nm)" package="0603 [SMD]"]
  LED2 = smd LED [color="Yellow (585nm)" package="0603 [SMD]"]
  LED3 = smd LED [color="Green (555nm)" package="0603 [SMD]"]
  R2 = Resistor [tolerance=±5% power=0.25W resistance=150 package=THT]
  R3 = Resistor [tolerance=±5% power=0.25W resistance=150 package=THT]
  R4 = Resistor [tolerance=±5% power=0.25W resistance=150 package=THT]
  M1 = HopeRF RFM9xW Breakout Board
  microSD1 = MicroSD Card Module
  S1 = Pushbutton [package="[THT]"]

nets:
  GND: Componente1.GND, A1.GND, LED1.cathode, LED2.cathode, LED3.cathode, M1.GND, microSD1.GND, S1.Pin_1, S1.Pin_2
  N1: Componente1.D2, A1.Rx
  N2: Componente1.D3, A1.Tx
  N3: Componente1.D4, microSD1.CS
  N4: Componente1.D5, R4.Pin_1
  N5: Componente1.D6, R3.Pin_1
  N6: Componente1.D7, R2.Pin_1
  N7: Componente1.D8, M1.DIO2
  N8: Componente1.D9, M1.RESET
  N9: Componente1.D10, M1.NSS
  N10: Componente1.D11/MOSI, M1.MOSI, microSD1.MOSI
  N11: Componente1.D12/MISO, M1.MISO, microSD1.MISO
  N12: Componente1.RESET, S1.Pin_3, S1.Pin_4
  VCC: Componente1.5V, A1.Vcc, microSD1.VCC
  3V3: Componente1.3V3, M1.3V3
  N13: Componente1.D13/SCK, M1.SCK, microSD1.SCK
  N14: LED1.anode, R2.Pin_0
  N15: LED2.anode, R4.Pin_0
  N16: LED3.anode, R3.Pin_0

notes:
  RESET

custom parts:
  NEO-6M GPS Module: GY-GPS6MV2 NEO-6M GPS Module Module based on U-blox NEO-6M GPS engine, incorporating regulator for 3.3-5V DC input, MS621FE-compatible rechargeable battery for backup and EEPROM for storing configuration settings. Links: NEO-6 series product information page NEO-6 Datasheet
  HopeRF RFM9xW Breakout Board: HopeRF RFM9xW module breakout board
  MicroSD Card Module: A common microSD card module.
