# Fritzing sketch tranmissor_lora_blocos (saved by Fritzing 1.0.2b)
breadboards: 1

parts:
  Componente1 = Arduino Nano (Rev3.0)
  U1 = LCD-16X2 [package=lcd-16x2_nosilk]
  A1 = NEO-6M GPS Module [part_number=GY-GPS6MV2]
  S1 = Momentary Switch [package=ksa_sealed_tac_switch]
  R1 = Resistor [tolerance=±5% power=0.25W resistance=330 package=THT]
  LCM1602_IIC1 = LCM1602 IIC [part_number="LCM1602 IIC" chip_label="LCM1602 IIC" package="DIP (Dual Inline) [THT]"]
  LED1 = smd LED [color="Red (633nm)" package="0603 [SMD]"]
  LED2 = smd LED [color="Yellow (585nm)" package="0603 [SMD]"]
  LED3 = smd LED [color="Green (555nm)" package="0603 [SMD]"]
  R2 = Resistor [tolerance=±5% power=0.25W resistance=150 package=THT]
  R3 = Resistor [tolerance=±5% power=0.25W resistance=150 package=THT]
  R4 = Resistor [tolerance=±5% power=0.25W resistance=150 package=THT]
  M1 = HopeRF RFM9xW Breakout Board
  BUZZER = Buzzer 12mm [part_number=COM-07950 package=buzzer-12mm-ns]
  S2 = Pushbutton [package="[THT]"]

nets:
  GND: Componente1.GND, Componente1.D12/MISO, A1.GND, S1.2, LCM1602_IIC1.GND, LED1.cathode, LED2.cathode, LED3.cathode, M1.GND, M1.MISO, BUZZER.2, S2.Pin_1, S2.Pin_2
  N1: Componente1.D2, A1.Rx
  N2: Componente1.D3, A1.Tx
  N3: Componente1.D4, S1.4
  N4: Componente1.D5, R4.Pin_1
  N5: Componente1.D6, R3.Pin_1
  N6: Componente1.D7, R2.Pin_1
  N7: Componente1.D8, M1.DIO2
  N8: Componente1.D9, M1.RESET
  N9: Componente1.D10, M1.NSS
  N10: Componente1.D11/MOSI, M1.MOSI
  N11: Componente1.RESET, S2.Pin_3, S2.Pin_4
  VCC: Componente1.5V, A1.Vcc, LCM1602_IIC1.VCC
  N12: Componente1.A5, LCM1602_IIC1.SCL
  N13: Componente1.A4, LCM1602_IIC1.SDA
  N14: Componente1.A3, Componente1.A2, BUZZER.1
  3V3: Componente1.3V3, M1.3V3, M1.DIO0
  N15: Componente1.D13/SCK, M1.SCK
  VSS: U1.VSS, LCM1602_IIC1.VSS
  VDD: U1.VDD, LCM1602_IIC1.VDD
  N16: U1.VO, LCM1602_IIC1.V0
  N17: U1.RS, LCM1602_IIC1.RS
  N18: U1.R_W, LCM1602_IIC1.RW
  N19: U1.E, LCM1602_IIC1.E
  N20: U1.DB0, LCM1602_IIC1.D0
  N21: U1.DB1, LCM1602_IIC1.D1
  N22: U1.DB2, LCM1602_IIC1.D2
  N23: U1.DB3, LCM1602_IIC1.D3
  N24: U1.DB4, LCM1602_IIC1.D4
  N25: U1.DB5, LCM1602_IIC1.D5
  N26: U1.DB6, LCM1602_IIC1.D6
  N27: U1.DB7, LCM1602_IIC1.D7
  N28: U1.A, LCM1602_IIC1.A
  N29: U1.K, LCM1602_IIC1.K
  N30: R1.Pin_0, LCM1602_IIC1.LED_B
  N31: R1.Pin_1, LCM1602_IIC1.LED_A
  N32: LED1.anode, R2.Pin_0
  N33: LED2.anode, R4.Pin_0
  N34: LED3.anode, R3.Pin_0

notes:
  Botão-Enviar
  BUZZER
  RESET

custom parts:
  NEO-6M GPS Module: GY-GPS6MV2 NEO-6M GPS Module Module based on U-blox NEO-6M GPS engine, incorporating regulator for 3.3-5V DC input, MS621FE-compatible rechargeable battery for backup and EEPROM for storing configuration settings. Links: NEO-6 series product information page NEO-6 Datasheet
  LCM1602 IIC: I2C-Module to use a 1602 or 2004 LCD on with the wire.h libory Serial LCD Modul
  HopeRF RFM9xW Breakout Board: HopeRF RFM9xW module breakout board
  Buzzer 12mm: Buzzer 12mm Spark Fun Electronics SKU : Comp-Buzzer Through hole This is a small 12mm round speaker that operates around the audible 2kHz range. You can use these speakers to create simple music or user interfaces. This is not a true piezoelectric speaker but behaves similarly. Instead of a piezoelectric crystal that vibrates with an electric current, this tiny speaker uses an electromagnet to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
