# Fritzing sketch end_device_class_a (saved by Fritzing 1.0.2b)
breadboards: 1

parts:
  Mod1 = Heltec WiFi LoRa 32 V2 [part_number=HTIT-WB32LA]
  DHT1 = DHT11 Humitidy and Temperature Sensor
  LED1 = LED - 5mm [color="Red (633nm)" current=0.030A package="5 mm [THT]"]
  LED2 = LED - 5mm [color="Yellow (585nm)" current=0.030A package="5 mm [THT]"]
  LED3 = LED - 5mm [color="Green (555nm)" current=0.030A package="5 mm [THT]"]
  R1 = Resistor [tolerance=±5% power=0.25W resistance=150 package=THT]
  R2 = Resistor [tolerance=±5% power=0.25W resistance=150 package=THT]
  R3 = Resistor [tolerance=±5% power=0.25W resistance=150 package=THT]

nets:
  N1: Mod1.pin_2, R2.Pin_1
  N2: Mod1.pin_3, R1.Pin_1
  N3: Mod1.pin_17, DHT1.VDD
  GND: Mod1.GND, DHT1.GND, LED1.cathode, LED2.cathode, LED3.cathode
  N4: Mod1.pin_29, R3.Pin_1
  N5: Mod1.pin_35, DHT1.DATA
  N6: LED1.anode, R3.Pin_0
  N7: LED2.anode, R2.Pin_0
  N8: LED3.anode, R1.Pin_0

custom parts:
  DHT11 Humitidy and Temperature Sensor: DHT11 Humidity and Temperature Sensor
