# Fritzing sketch end_device_class_c (saved by Fritzing 1.0.2b)

parts:
  Mod1 = Heltec WiFi LoRa 32 V2 [part_number=HTIT-WB32LA]
  LED1 = LED - 5mm [color="Red (633nm)" current=0.030A package="5 mm [THT]"]
  M1 = BME280
  R1 = Resistor [tolerance=±5% power=0.25W resistance=150 package=THT]

nets:
  N1: Mod1.pin_1, M1.SDA
  N2: Mod1.pin_20, M1.VIN
  N3: Mod1.pin_27, M1.SCL
  N4: Mod1.pin_29, R1.Pin_0
  N5: LED1.cathode, M1.GND

custom parts:
  BME280: Temperature Humidity Barometric presure Sensor
