# Fritzing sketch end_device_movel (saved by Fritzing 1.0.2b)
# 18650 Li-ion Battery: CC-BY Dr Kristofer Chan, King's College London/Remote-research.org

parts:
  S1 = Toggle Switch [package=THT]
  S2 = Pushbutton [package="[THT]"]
  Mod1 = Heltec WiFi LoRa 32 V2 [part_number=HTIT-WB32LA]
  A1 = NEO-6M GPS Module [part_number=GY-GPS6MV2]
  LED1 = LED - 5mm [color="Green (555nm)" current=0.030A package="5 mm [THT]"]
  BAT1 = 18650 Li-ion Battery [package=battery-18650]
  R1 = Resistor [tolerance=±5% resistance=150 package="0805 [SMD]"]
  Harwin_M40-1 = Connector M40-1100300 [form="♀ (female)"]
  U1 = Mini-360 DC-DC Buck converter [package=THT]

nets:
  N1: S1.COM, Mod1.pin_16, Mod1.pin_17, U1.IN+
  N2: S1.L2, BAT1.+, Harwin_M40-1.pin3
  N3: S2.Pin_1, S2.Pin_2, Mod1.GND, LED1.cathode, BAT1.-, Harwin_M40-1.Circuit_1, U1.IN-
  N4: S2.Pin_3, S2.Pin_4, Mod1.pin_26
  N5: Mod1.pin_7, R1.Pin_1
  N6: Mod1.pin_33, A1.Tx
  N7: Mod1.pin_35, A1.Rx
  N8: A1.GND, U1.OUT-
  N9: A1.Vcc, U1.OUT+

notes:
  HW-045
  ON
  OFF
  Conector JST 2
  Enviar
  O conector JST 2 está conectado na PCB do MCU, pois existe um BMS para 1 célula de lítio
  O converter foi usado para aumentar a tensão de entrada de 3,3V para 5V. Ouve uma melhora do módulo GPS em triangular satélites.

custom parts:
  NEO-6M GPS Module: GY-GPS6MV2 NEO-6M GPS Module Module based on U-blox NEO-6M GPS engine, incorporating regulator for 3.3-5V DC input, MS621FE-compatible rechargeable battery for backup and EEPROM for storing configuration settings. Links: NEO-6 series product information page NEO-6 Datasheet
  18650 Li-ion Battery: 18650 li-ion Battery Standard 18650 battery with interactive connectors Creative Common Attribution 4.0 International (CC-BY 4.0) license. Any use of this part requires attribution of Dr Kristofer Chan, Department of Geography, King's College London. Contact kristofer.chan [at] kcl.ac.uk OR kris [at] remote-research.org for further information.
  Mini-360 DC-DC Buck converter: Mini-360 DC-DC Buck converter. Tiny buck step down voltage converter, input voltage 4.75 to 23V output 1 to 17V adjustable. Available from ebay and the like.
